# Fritzing sketch breadboard_NANO (saved by Fritzing 0.9.3b)
breadboards: 1

parts:
  Part1 = Arduino Nano (Rev3.0)
  Pololu_A1 = Pololu A4988 [package=SO16]
  R2 = Rotary Potentiometer (Small) [maximum_resistance=100kΩ package=THT]
  C1 = Electrolytic Capacitor [capacitance=100μF voltage=50V package="0807 [SMD, electrolytic]"]
  endstop_1 = Round Pushbutton
  endstop_2 = Round Pushbutton
  M1 = Stepper Motor - Bipolar

nets:
  N1: Part1.GND, Pololu_A1.ENABLE, Pololu_A1.GND#8, R2.leg2, C1.-, endstop_1.leg1, endstop_2.leg1
  N2: Part1.D2, endstop_2.leg0
  N3: Part1.D3, endstop_1.leg0
  N4: Part1.D4, Pololu_A1.DIR
  N5: Part1.D5, Pololu_A1.STEP
  N6: Part1.VIN, Pololu_A1.VMOT
  5V: Part1.5V, Pololu_A1.MS1, Pololu_A1.MS2, Pololu_A1.VDD, R2.leg1
  N7: Part1.A1, R2.wiper, C1.+
  N8: Pololu_A1.RESET, Pololu_A1.SLEEP
  N9: Pololu_A1.1B, M1.D
  N10: Pololu_A1.1A, M1.B
  N11: Pololu_A1.2A, M1.C
  N12: Pololu_A1.2B, M1.A
